# Fritzing sketch luz led (saved by Fritzing 0.9.5d)
breadboards: 1

parts:
  Componente1 = Arduino Uno (Rev3)
  LED1 = LED - 5mm [color="Red (633nm)" package="5 mm [THT]"]
  R1 = Resistor [tolerance=±5% resistance=220 package=THT]
  Componente2 = Arduino Uno (Rev3)
  R2 = Resistor [tolerance=±5% resistance=220 package=THT]
  LED2 = LED - 5mm [color="Red (633nm)" package="5 mm [THT]"]
  LED3 = LED - 5mm [color="Yellow (592nm)" package="5 mm [THT]"]

nets:
  N1: Componente1.D13/SCK, LED1.anode
  N2: Componente1.GND, R1.Pin_1
  N3: LED1.cathode, R1.Pin_0
  N4: Componente2.D12/MISO, LED3.anode
  N5: Componente2.D13/SCK, LED2.anode
  N6: Componente2.GND, R2.Pin_0
  N7: R2.Pin_1, LED2.cathode, LED3.cathode

notes:
  Ejemplo 1
  Ejemplo 2
