# Fritzing sketch servo (saved by Fritzing 0.9.5d)
breadboards: 1

parts:
  J1 = Basic Servo
  Componente1 = Arduino Uno (Rev3)

nets:
  GND: J1.gnd, Componente1.GND
  VCC: J1.vcc, Componente1.5V
  N1: J1.pulse, Componente1.D9_PWM
